# Fritzing sketch esp_mcp_lf (saved by Fritzing 0.9.2b)
breadboards: 1

parts:
  Espessif_Serial_Wifi_Modul_1 = ESP8266 ESP01 [part_number=ESP8266 package=THT]
  U1 = Voltage Regulator - 3.3V [part_number=LF33 package="TO220 [THT]"]
  V1 = DC Power [voltage=5]
  J1 = female pin header, 10 pins [form="♀ (female)" part_number=PinOut9-16]
  IC1 = MCP23017 I2C I/O Expander [part_number=MCP23017]
  J2 = female pin header, 10 pins [form="♀ (female)" part_number=PinOut9-16]
  J3 = female pin header, 5 pins [form="♀ (female)" part_number="UART Connector"]  # not connected

nets:
  GND: Espessif_Serial_Wifi_Modul_1.GND, U1.GND, V1.V-, J1.pin1, J1.pin10, IC1.VSS, IC1.A0, IC1.A1, IC1.A2, J2.pin1, J2.pin10
  VCC: Espessif_Serial_Wifi_Modul_1.VCC, Espessif_Serial_Wifi_Modul_1.CH_PD, U1.output_voltage, IC1.VDD, IC1.RESET
  N1: Espessif_Serial_Wifi_Modul_1.GPIO00, IC1.SCL
  N2: Espessif_Serial_Wifi_Modul_1.GPIO02, IC1.SDA
  N3: U1.input_voltage, V1.V+
  N4: J1.pin2, IC1.GPA0
  N5: J1.pin3, IC1.GPA1
  N6: J1.pin4, IC1.GPA2
  N7: J1.pin5, IC1.GPA3
  N8: J1.pin6, IC1.GPA4
  N9: J1.pin7, IC1.GPA5
  N10: J1.pin8, IC1.GPA6
  N11: J1.pin9, IC1.GPA7
  N12: IC1.GPB0, J2.pin2
  N13: IC1.GPB1, J2.pin3
  N14: IC1.GPB2, J2.pin4
  N15: IC1.GPB3, J2.pin5
  N16: IC1.GPB4, J2.pin6
  N17: IC1.GPB5, J2.pin7
  N18: IC1.GPB6, J2.pin8
  N19: IC1.GPB7, J2.pin9

custom parts:
  ESP8266 ESP01: Generic WiFi Module based on the ESP8266 with onboard PCB antenna and UART communications
  MCP23017 I2C I/O Expander: The MCP23017 uses two i2c pins (these can be shared with other i2c devices), and in exchange gives you 16 general purpose pins. You can set each of 16 pins to be input, output, input with a pullup or open drain. There's even the ability to get an interrupt via an external pin when any of the inputs change so you don't have to keep polling the chip.
